# Fritzing sketch Minikeyboard (saved by Fritzing 0.9.3b)
breadboards: 1

parts:
  Part1 = Arduino Nano (Rev3.0)
  S1 = Momentary Switch [package=ksa_sealed_tac_switch]
  S2 = Momentary Switch [package=ksa_sealed_tac_switch]
  S3 = Momentary Switch [package=ksa_sealed_tac_switch]
  S4 = Momentary Switch [package=ksa_sealed_tac_switch]

nets:
  N1: Part1.GND, S1.4, S2.4, S3.4, S4.4
  N2: Part1.D2, S1.1
  N3: Part1.D3, S2.1
  N4: Part1.D4, S3.1
  N5: Part1.D5, S4.1
